// Logisim project Logisim_Schematic.circ as structural Verilog: 1 circuit, main circuit main
module main (
  input  [3:0] in_1,
  input  [3:0] in_2,
  input  in_3,
  output [3:0] Output
);

  Multiplexer #(.enable("false")) multiplexer_1 (.in0(in_1[0]), .in1(in_2[0]), .out(Output[0]), .sel(in_3));
  Multiplexer #(.disabled(0), .enable("false")) multiplexer_2 (
    .in0(in_1[1]), .in1(in_2[1]), .out(Output[1]), .sel(in_3));
  Multiplexer #(.enable("false")) multiplexer_3 (.in0(in_1[2]), .in1(in_2[2]), .out(Output[2]), .sel(in_3));
  Multiplexer #(.enable("false")) multiplexer_4 (.in0(in_1[3]), .in1(in_2[3]), .out(Output[3]), .sel(in_3));

  // Other names for the same wires on the sheet: M_1 = in_1[0]; M_2 = in_1[1]; M_3 = in_1[2]; M_4 = in_1[3];
  //   m_1_t = in_2[0]; m_2_t = in_2[1]; m_3_t = in_2[2]; m_4_t = in_2[3]; F_1 = Output[0]; F_2 = Output[1];
  //   F_3 = Output[2]; F_4 = Output[3]; Switch = in_3

  // Notes on the sheet:
  //   Input 1
  //   Input 2
  //   Lab 1: 2 to 1 Multiplexer 4-bit
endmodule
