// Logisim project Schematic for Lab 2.circ as structural Verilog: 1 circuit, main circuit main
module main (
  input  A,
  input  B,
  input  A_2,
  input  B_2,
  input  C,
  input  D,
  input  A_3,
  input  E,
  input  B_3,
  input  A_4,
  input  B_4
);

  wire _0, _0A, _0B, _0C, _0D, _0E, _0F, _1, _2, _3, _4, _5, _6, _7, _8, _9, E1, E2, E3, E4;

  Decoder #(.select(2)) decoder_1 (.out0(E1), .out1(E2), .out2(E3), .out3(E4), .sel({C, D}), .en(E));
  Decoder #(.select(2)) decoder_2 (.out0(_0), .out1(_1), .out2(_2), .out3(_3), .sel({A, B}), .en(E1));
  Decoder #(.select(2)) decoder_3 (.out0(_4), .out1(_5), .out2(_6), .out3(_7), .sel({A_2, B_2}), .en(E2));
  Decoder #(.select(2)) decoder_4 (.out0(_8), .out1(_9), .out2(_0A), .out3(_0B), .sel({A_3, B_3}), .en(E3));
  Decoder #(.select(2)) decoder_5 (.out0(_0C), .out1(_0D), .out2(_0E), .out3(_0F), .sel({A_4, B_4}), .en(E4));

  // Notes on the sheet:
  //   Lab 3: 4 to 16 Decoder
endmodule
