// Logisim project Full Adder Schematic.circ as structural Verilog: 1 circuit, main circuit main
module main (
  input  in_1,
  input  in_2,
  input  in_3,
  input  in_4,
  input  in_5,
  input  in_6,
  input  in_7,
  input  in_8,
  input  in_9,
  input  in_10,
  input  in_11,
  input  in_12,
  input  in_13,
  input  in_14,
  input  in_15,
  input  in_16,
  input  in_17,
  input  in_18,
  output [15:0] out_19,
  output [15:0] out_20,
  output out_21,
  output [15:0] out_22
);

  wire button_1_out, button_2_out;
  wire [15:0] demultiplexer_1_out0, demultiplexer_1_out1;

  Demultiplexer #(.width(16), .enable("false")) demultiplexer_1 (
    .out0(demultiplexer_1_out0), .out1(demultiplexer_1_out1),
    .in({in_18, in_17, in_16, in_15, in_14, in_13, in_12, in_11, in_10, in_9, in_8, in_6, in_5, in_4, in_3, in_2}),
    .sel(in_7));
  Register #(.width(16)) register_1 (.D(demultiplexer_1_out0), .Q(out_19), .clk(button_1_out));  // open: en, clr
  Button button_1 (.out(button_1_out));
  Register #(.width(16)) register_2 (.D(demultiplexer_1_out1), .Q(out_22), .clk(button_2_out));  // open: en, clr
  Button button_2 (.out(button_2_out));
  Adder #(.width(16)) adder_1 (.a(out_19), .b(out_22), .out(out_20), .cin(in_1), .cout(out_21));

  // Notes on the sheet:
  //   Lab 4: Full Adder
endmodule
